# Fritzing sketch step_poten (saved by Fritzing 0.9.3b)
breadboards: 1

parts:
  부품1 = Arduino Nano (Rev3.0)
  IC1 = ULN2003A [package="DIP16 [THT]"]
  R1 = Rotary Potentiometer (Large) [maximum_resistance=100kΩ package=THT]

nets:
  N1: 부품1.D2, IC1.In_1
  N2: 부품1.D3, IC1.In_2
  N3: 부품1.D4, IC1.In_3
  N4: 부품1.D5, IC1.In_4
  N5: 부품1.A0, R1.wiper
  N6: IC1.0V, R1.leg2
  N7: IC1.COM_-_Common, R1.leg1
